# Fritzing sketch matrix (saved by Fritzing 0.8.5b)
breadboards: 1

parts:
  U1 = ESP8266 WiFi Module [part_number=ESP8266]
  Part1 = FTDI Basic Programmer
  8x8_LED_matrix_MAX1 = 8x8 Red 8x8 LED Matrix with MAX7219
  8x8_LED_matrix_MAX2 = 8x8 Red 8x8 LED Matrix with MAX7219
  8x8_LED_matrix_MAX3 = 8x8 Red 8x8 LED Matrix with MAX7219

nets:
  N1: U1.RXD, Part1.TXO
  VCC: U1.VCC, U1.CH_PD, 8x8_LED_matrix_MAX1.VCC, 8x8_LED_matrix_MAX1.VCC_PT, 8x8_LED_matrix_MAX2.VCC, 8x8_LED_matrix_MAX2.VCC_PT, 8x8_LED_matrix_MAX3.VCC, 8x8_LED_matrix_MAX3.VCC_PT
  GND: U1.GPIO_0, U1.GND, U1.GPIO_15, Part1.GND, 8x8_LED_matrix_MAX1.GND, 8x8_LED_matrix_MAX1.CLK_PT, 8x8_LED_matrix_MAX2.GND_PT, 8x8_LED_matrix_MAX2.CLK, 8x8_LED_matrix_MAX3.GND, 8x8_LED_matrix_MAX3.CLK_PT
  N2: U1.GPIO_2, 8x8_LED_matrix_MAX1.DIN_CHN, 8x8_LED_matrix_MAX1.CS, 8x8_LED_matrix_MAX2.DIN
  N3: U1.TXD, Part1.RXI
  N4: U1.GPIO_14, 8x8_LED_matrix_MAX1.GND_PT, 8x8_LED_matrix_MAX1.CLK, 8x8_LED_matrix_MAX2.GND, 8x8_LED_matrix_MAX2.CLK_PT, 8x8_LED_matrix_MAX3.CLK
  N5: U1.GPIO_13, 8x8_LED_matrix_MAX1.DIN
  N6: 8x8_LED_matrix_MAX1.CS_PT, 8x8_LED_matrix_MAX2.DIN_CHN, 8x8_LED_matrix_MAX2.CS, 8x8_LED_matrix_MAX3.DIN
  N7: 8x8_LED_matrix_MAX2.CS_PT, 8x8_LED_matrix_MAX3.CS

custom parts:
  ESP8266 WiFi Module: Generic WiFi Module based on the ESP8266 with onboard PCB antenna and UART communications
  8x8 Red 8x8 LED Matrix with MAX7219: Description: 8 by 8 red LED matrix with a MAX7219 controller.
